// Logisim project addsub.circ as structural Verilog
module main (
  input  [3:0] in_1,
  input  [3:0] in_2,
  output out_3,
  output out_4,
  output out_5,
  output out_6,
  output out_7
);

  adder4bit adder4bit_1 (
    .b3(in_1[3]), .b2(in_1[2]), .b1(in_1[1]), .b0(in_1[0]), .a3(in_2[3]), .a2(in_2[2]), .a1(in_2[1]),
    .a0(in_2[0]), .rout(out_3), .y3(out_4), .y2(out_5), .y1(out_6), .y0(out_7));
endmodule

module decoder2bit (
  input  s1,
  input  s0,
  output y0,
  output y1,
  output y2,
  output y3
);

  and and_1 (y0, ~s1, ~s0);  // AND_Gate
  and and_2 (y1, ~s1, s0);  // AND_Gate
  and and_3 (y2, s1, ~s0);  // AND_Gate
  and and_4 (y3, s1, s0);
endmodule

module andBitwise4 (
  input  b4,
  input  a3,
  input  b2,
  input  a2,
  input  b1,
  input  a1,
  input  b0,
  input  a0,
  output y3,
  output y2,
  output y1,
  output y0
);

  and and_1 (y3, b4, a3);
  and and_2 (y2, b2, a2);
  and and_3 (y1, b1, a1);
  and and_4 (y0, b0, a0);
endmodule

module multiplexer4bit (
  input  [3:0] x,
  input  s1,
  input  s0,
  output y
);

  wire andbitwise4_1_y0, andbitwise4_1_y1, andbitwise4_1_y2, andbitwise4_1_y3;
  wire [3:0] decoder2bit_1_y0;

  decoder2bit decoder2bit_1 (
    .s1(s1), .s0(s0), .y0(decoder2bit_1_y0[0]), .y1(decoder2bit_1_y0[1]), .y2(decoder2bit_1_y0[2]),
    .y3(decoder2bit_1_y0[3]));
  andBitwise4 andbitwise4_1 (
    .b4(x[3]), .a3(decoder2bit_1_y0[3]), .b2(x[2]), .a2(decoder2bit_1_y0[2]), .b1(x[1]),
    .a1(decoder2bit_1_y0[1]), .b0(x[0]), .a0(decoder2bit_1_y0[0]), .y3(andbitwise4_1_y3),
    .y2(andbitwise4_1_y2), .y1(andbitwise4_1_y1), .y0(andbitwise4_1_y0));
  or or_1 (y, andbitwise4_1_y3, andbitwise4_1_y2, andbitwise4_1_y1, andbitwise4_1_y0);
endmodule

module halfadder (
  input  a,
  input  b,
  output r,
  output y
);

  and and_1 (r, a, b);
  xor xor_1 (y, a, b);
endmodule

module fulladder (
  input  rin,
  input  a,
  input  b,
  output rout,
  output y
);

  wire halfadder_1_r, halfadder_1_y, halfadder_2_r;

  halfadder halfadder_1 (.a(a), .b(b), .r(halfadder_1_r), .y(halfadder_1_y));
  halfadder halfadder_2 (.a(rin), .b(halfadder_1_y), .r(halfadder_2_r), .y(y));
  or or_1 (rout, halfadder_1_r, halfadder_2_r);
endmodule

module adder4bit (
  input  b3,
  input  b2,
  input  b1,
  input  b0,
  input  a3,
  input  a2,
  input  a1,
  input  a0,
  output rout,
  output y3,
  output y2,
  output y1,
  output y0
);

  wire fulladder_2_rout, fulladder_3_rout, halfadder_1_r;

  fulladder fulladder_1 (.rin(fulladder_2_rout), .a(b3), .b(a3), .rout(rout), .y(y3));
  fulladder fulladder_2 (.rin(fulladder_3_rout), .a(b2), .b(a2), .rout(fulladder_2_rout), .y(y2));
  fulladder fulladder_3 (.rin(halfadder_1_r), .a(b1), .b(a1), .rout(fulladder_3_rout), .y(y1));
  halfadder halfadder_1 (.a(b0), .b(a0), .r(halfadder_1_r), .y(y0));
endmodule

module complemento1 (
  input  a3,
  input  a2,
  input  a1,
  input  a0,
  output y3,
  output y2,
  output y1,
  output y0
);

  not not_1 (y3, a3);
  not not_2 (y2, a2);
  not not_3 (y1, a1);
  not not_4 (y0, a0);
endmodule

module complemento2 (
  input  a3,
  input  a2,
  input  a1,
  input  a0,
  output rout,
  output y3,
  output y2,
  output y1,
  output y0
);

  wire complemento1_1_y0, complemento1_1_y1, complemento1_1_y2, complemento1_1_y3;

  complemento1 complemento1_1 (
    .a3(a3), .a2(a2), .a1(a1), .a0(a0), .y3(complemento1_1_y3), .y2(complemento1_1_y2),
    .y1(complemento1_1_y1), .y0(complemento1_1_y0));
  incr1for4bit incr1for4bit_1 (
    .a3(complemento1_1_y3), .a2(complemento1_1_y2), .a1(complemento1_1_y1), .a0(complemento1_1_y0), .i(1'b1),
    .rout(rout), .y3(y3), .y2(y2), .y1(y1), .y0(y0));
endmodule

module incr1for4bit (
  input  a3,
  input  a2,
  input  a1,
  input  a0,
  input  i,
  output rout,
  output y3,
  output y2,
  output y1,
  output y0
);

  wire halfadder_2_r, halfadder_3_r, halfadder_4_r;

  halfadder halfadder_1 (.a(a3), .b(halfadder_2_r), .r(rout), .y(y3));
  halfadder halfadder_2 (.a(a2), .b(halfadder_3_r), .r(halfadder_2_r), .y(y2));
  halfadder halfadder_3 (.a(a1), .b(halfadder_4_r), .r(halfadder_3_r), .y(y1));
  halfadder halfadder_4 (.a(a0), .b(i), .r(halfadder_4_r), .y(y0));
endmodule
